# Fritzing sketch power-circuit-mini-mint (saved by Fritzing 0.9.3b)
breadboards: 2

parts:
  Part5 = Adafruit PowerBoost 1000C [part_number="Adafruit #2465"]
  Part7 = Adafruit AT42QT1010 Standalone Momentary Capacitive Touch Sensor [part_number="Adafruit #1374"]
  R7 = Resistor [tolerance=±5% resistance=10k package=THT]
  Q8 = NPN-Transistor [package="TO92 [THT]"]
  C3 = Capacitor [package=cap-pth-small2]
  C4 = Capacitor [package=cap-pth-small2]
  Q9 = NPN-Transistor [package="TO92 [THT]"]
  R8 = Resistor [tolerance=±5% resistance=100k package=THT]
  R9 = Resistor [tolerance=±5% resistance=100k package=THT]
  Q10 = NPN-Transistor [package="TO92 [THT]"]
  Q11 = NPN-Transistor [package="TO92 [THT]"]
  R10 = Resistor [tolerance=±5% resistance=100k package=THT]
  Part6 = INA219 High Side DC Current Sensor Breakout [part_number=904]
  S2 = Momentary Switch [package=ksa_sealed_tac_switch]
  JP1 = USB_MICROB_PLUG [package=micro-b-th]
  U1 = Molex Picoblade Series Header [part_number=0533980271 package=Picoblade-53398-0271]
  U5 = Molex Picoblade Series Header [part_number=0533980271 package=Picoblade-53398-0271]  # not connected
  Part8 = Lithium Ion Polymer Battery 3.7v 2500mAh [part_number=328]
  IC5 = IC, DIP package, 14 pins [chip_label=74AHCT125]
  DOTSTAR1 = DotStar Strip -- White (60/m) [part_number=2240]
  U3 = Molex Picoblade Series Header [part_number=0533980571 package=Picoblade-53398-0571]
  U4 = Molex Picoblade Series Header [part_number=0533980571 package=Picoblade-53398-0571]

nets:
  GND: Part5.GND, Part7.GND, C4.1, Q9.E, Q10.E, Q11.E, Part6.GND, JP1.GND, Part8.negative, IC5.pin1, IC5.pin4, IC5.pin7, DOTSTAR1.GND
  VCC: Part5.5.0V, Part6.VCC, JP1.VCC, IC5.pin14, DOTSTAR1.+5V
  N1: Part5.VLIPO, Part6.VIN-
  N2: Part5.ENABLE, Q11.C
  N3: Part7.VDD, R9.Pin_0, Part6.VIN+, Part8.positive
  N4: Part7.OUT, R7.Pin_0, R8.Pin_0
  N5: R7.Pin_1, Q8.B, C3.2
  N6: Q8.E, C3.1, U3.2
  N7: Q8.C, U3.3
  N8: C4.2, Q9.B, R8.Pin_1
  N9: Q9.C, R9.Pin_1, Q10.C, Q11.B
  N10: Q10.B, R10.Pin_1
  N11: R10.Pin_0, U3.1
  N12: Part6.SCL, U1.2
  N13: Part6.SDA, U1.1
  N14: S2.1, U4.3
  N15: S2.3, U4.2
  N16: IC5.pin2, U3.5
  N17: IC5.pin3, DOTSTAR1.CI
  N18: IC5.pin5, U3.4
  N19: IC5.pin6, DOTSTAR1.DI

notes:
  Pins are for the Qi charger
  Cyan > GPIO (DotStar data/clock)
  Orange > GPIO (DotStar data/clock)
  Brown+Ochre > OnOff shim button
  Purple > 3.3v from RPi (hold power on)
  White > SCL
  Blue > SDA
  Power to Raspberry Pi via OnOff shim

custom parts:
  Adafruit PowerBoost 1000C: PowerBoost 1000C is the perfect power supply for your portable project! With a built-in load-sharing battery charger circuit, you'll be able to keep your power-hungry project running even while recharging the battery! This little DC/DC boost converter module can be powered by any 3.7V LiIon/LiPoly battery, and convert the battery output to 5.2V DC for running your 5V projects.
  Adafruit AT42QT1010 Standalone Momentary Capacitive Touch Sensor: This breakout board is the simplest way to create a project with a single "momentary" capacitive touch sensor. No microcontroller is required here - just power with 1.8 to 5.5VDC and touch the pad to activate the sensor. When a capacitive load is detected (e.g. a person touches the sensor-pad area) the red LED lights up and the output pin goes high. You can also solder a wire to the middle pad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
  INA219 High Side DC Current Sensor Breakout: This breakout board will solve all your power-monitoring problems. Instead of struggling with two multimeters, you can just use the handy INA219B chip on this breakout to both measure both the high side voltage and DC current draw over I2C with 1% precision. Most current-measuring devices such as our current panel meter are only good for low side measuring. That means that unless you want to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
  Lithium Ion Polymer Battery 3.7v 2500mAh: Lithium ion polymer (also known as 'lipo' or 'lipoly') batteries are thin, light and powerful. The output ranges from 4.2V when completely charged to 3.7V. This battery has a capacity of 2500mAh for a total of about 10 Wh. The batteries come pre-attached with a genuine 2-pin JST-PH connector as shown and include the necessary protection circuitry.
  DotStar Strip -- White (60/m): NeopixelDotStar Strip, White, 60 pixels per meter.
