# Fritzing sketch sensor-rail-mini-mint (saved by Fritzing 0.9.3b)
breadboards: 7

parts:
  IC3 = MCP23017 I2C I/O Expander
  Part35 = Adafruit TCA9548A
  Part37 = Adafruit TSL2591 [part_number="Adafruit #1980"]
  Part38 = Adafruit VEML6075 UV Sensor Breakout [part_number=3964]
  Part39 = Adafruit TCS34725 RGB Color Sensor [part_number="Adafruit #1334"]
  Part41 = Adafruit TSL2591 [part_number="Adafruit #1980"]
  Part42 = Adafruit VEML6075 UV Sensor Breakout [part_number=3964]
  U14 = Molex Picoblade Series Header [part_number=0533980671 package=Picoblade-53398-0671]
  U15 = Molex Picoblade Series Header [part_number=0533980371 package=Picoblade-53398-0371]
  Part43 = Adafruit TCS34725 RGB Color Sensor [part_number="Adafruit #1334"]
  U16 = MLX90614 [package=to-39]
  Part45 = Adafruit VL6180X Time of Flight Distance Sensor [part_number="Adafruit #3316"]
  U18 = Molex Picoblade Series Header [part_number=0533980471 package=Picoblade-53398-0471]
  Part46 = Adafruit SHT31-D Sensirion Temperature/Humidity Sensor [part_number="Adafruit #2857"]
  Part47 = Adafruit SGP30 Gas Sensor
  Part48 = Adafruit MLX90393 Magnetometer [part_number="Adafruit #4022"]
  Part49 = 9-DOF Absolute Orientation IMU Fusion Breakout - BNO055
  Q1 = Basic FET N-Channel [package="TO220 [THT]"]
  U19 = Molex Picoblade Series Header [part_number=0533980871 package=Picoblade-53398-0871]
  U17 = Molex Picoblade Series Header [part_number=0533980671 package=Picoblade-53398-0671]
  U22 = Molex Picoblade Series Header [part_number=0533980471 package=Picoblade-53398-0471]
  R11 = Resistor [tolerance=±5% resistance=100k package=THT]
  Q2 = Basic FET N-Channel [package="TO220 [THT]"]
  R12 = Resistor [tolerance=±5% resistance=100k package=THT]
  U20 = Molex Picoblade Series Header [part_number=0533980271 package=Picoblade-53398-0271]
  U21 = Molex Picoblade Series Header [part_number=0533980371 package=Picoblade-53398-0371]
  R14 = Resistor [tolerance=±5% resistance=4.7 package=THT]
  R15 = Resistor [tolerance=±5% resistance=4.7 package=THT]
  Part51 = TXB0104 4-channel Bi-Directional Level Shifter
  Part53 = Adafruit ADS1115 16Bit I2C ADC [part_number="Adafruit #1085"]
  Q3 = Basic FET N-Channel [package="TO220 [THT]"]
  U23 = Molex Picoblade Series Header [part_number=0533980471 package=Picoblade-53398-0471]
  Part54 = Adafruit BMP388 - Barometric Pressure and Altimeter [part_number="Adafruit #3966"]
  R17 = Resistor [tolerance=±5% resistance=100k package=THT]
  R18 = Resistor [tolerance=±5% resistance=100k package=THT]
  R19 = Resistor [tolerance=±5% resistance=100k package=THT]
  R20 = Resistor [tolerance=±5% resistance=100k package=THT]
  R21 = Resistor [tolerance=±5% resistance=100k package=THT]
  R22 = Resistor [tolerance=±5% resistance=100k package=THT]
  R23 = Resistor [tolerance=±5% resistance=100k package=THT]
  R24 = Resistor [tolerance=±5% resistance=100k package=THT]
  R25 = Resistor [tolerance=±5% resistance=100k package=THT]
  R26 = Resistor [tolerance=±5% resistance=100k package=THT]
  R27 = Resistor [tolerance=±5% resistance=100k package=THT]
  R28 = Resistor [tolerance=±5% resistance=100k package=THT]
  R29 = Resistor [tolerance=±5% resistance=100k package=THT]
  R30 = Resistor [tolerance=±5% resistance=100k package=THT]
  R31 = Resistor [tolerance=±5% resistance=100k package=THT]
  R32 = Resistor [tolerance=±5% resistance=100k package=THT]
  R33 = Resistor [tolerance=±5% resistance=100k package=THT]
  R34 = Resistor [tolerance=±5% resistance=100k package=THT]
  R35 = Resistor [tolerance=±5% resistance=100k package=THT]
  R36 = Resistor [tolerance=±5% resistance=100k package=THT]
  R37 = Resistor [tolerance=±5% resistance=100k package=THT]
  R38 = Resistor [tolerance=±5% resistance=100k package=THT]
  R39 = Resistor [tolerance=±5% resistance=100k package=THT]

nets:
  N1: IC3.GPB0, U17.2, Part51.A1, R25.Pin_0, R25.Pin_1
  N2: IC3.GPB1, U16.PWM_SDA, U17.3, R26.Pin_0, R26.Pin_1, R39.Pin_1
  N3: IC3.GPB2, U16.SCL_VZ, U17.4, R27.Pin_0, R27.Pin_1, R38.Pin_1
  N4: IC3.GPB3, Part45.GPIO, U17.5, R28.Pin_0, R28.Pin_1
  N5: IC3.GPB4, Part45.XSHUT, U17.6, R29.Pin_0, R29.Pin_1
  N6: IC3.GPB5, Part46.ALERT, R30.Pin_0, R30.Pin_1
  N7: IC3.GPB6, Part49.RST_5V, R31.Pin_0, R31.Pin_1
  N8: IC3.GPB7, Part54.INT, R32.Pin_0, R32.Pin_1
  VIN: IC3.VDD, Part35.VCC, Part38.VIN, Part39.VIN, Part42.VIN, U14.6, Part43.VIN, U16.VDD, Part45.VIN, U18.4, Part46.VIN, Part47.VIN, Part48.VIN, Part49.5.0V, Q1.drain, R14.Pin_1, R15.Pin_1, Part51.LV, Part54.VIN, R38.Pin_0, R39.Pin_0
  GND: IC3.VSS, Part35.GND, Part39.GND, U14.5, Part43.GND, U16.VSS, Part45.GND, U18.3, Part46.GND, Part47.GND, Part48.GND, Part49.GND, U19.4, U22.4, U21.3, Part51.GND, Part53.ADDR, Part53.GND, Part54.GND
  N9: IC3.SCL, Part35.INPUTSCL, U20.2, R15.Pin_0, U23.4
  N10: IC3.SDA, Part35.INPUTSDA, U20.1, R14.Pin_0, U23.3
  N11: IC3.A0, IC3.A1, IC3.A2
  N12: IC3.INTB, R37.Pin_0
  N13: IC3.INTA, R36.Pin_0
  N14: IC3.GPA0, Part48.INT_3V, R24.Pin_0, R24.Pin_1
  N15: IC3.GPA1, Part37.INT, R23.Pin_0, R23.Pin_1
  N16: IC3.GPA2, Part39.INT, R22.Pin_0, R22.Pin_1
  N17: IC3.GPA3, Part39.LED_EN, R21.Pin_0, R21.Pin_1
  N18: IC3.GPA4, Part41.INT, U15.1, R20.Pin_0, R20.Pin_1
  N19: IC3.GPA5, U15.2, Part43.INT, R19.Pin_0, R19.Pin_1
  N20: IC3.GPA6, U15.3, Part43.LED_EN, R17.Pin_0, R17.Pin_1
  N21: IC3.GPA7, R18.Pin_0, R18.Pin_1
  N22: Part35.2SDA, Part41.SDA, Part42.SDA, U14.1
  N23: Part35.2SCL, Part41.SCL, Part42.SCL, U14.2
  N24: Part35.3SDA, U14.3, Part43.SDA
  N25: Part35.3SCL, U14.4, Part43.SCL
  N26: Part35.4SDA, Part37.SDA, Part38.SDA
  N27: Part35.4SCL, Part37.SCL, Part38.SCL
  N28: Part35.5SDA, Part39.SDA
  N29: Part35.5SCL, Part39.SCL
  N30: Part35.6SDA, Part49.SDA_5V
  N31: Part35.6SCL, Part49.SCL_5V
  N32: Part35.7SDA, Part48.SDA
  N33: Part35.7SCL, Part48.SCL
  N34: Part35.RESET, U19.8, R33.Pin_0, R33.Pin_1
  N35: Part35.0SDA, Part46.SDA, Part47.SDA, Part53.SDA, Part54.SDI/SDA
  N36: Part35.0SCL, Part46.SCL, Part47.SCL, Part53.SCL, Part54.SCK/SCL
  N37: Part35.1SDA, Part45.SDA, U18.1, U22.2
  N38: Part35.1SCL, Part45.SCL, U18.2, U22.3
  N39: Q1.gate, R11.Pin_0
  N40: Q1.source, U19.3
  N41: U19.1, Q2.source
  N42: U19.2, R12.Pin_1
  N43: U19.5, R11.Pin_1
  N44: U19.6, R36.Pin_1
  N45: U19.7, R37.Pin_1
  N46: U17.1, U22.1, Q2.drain, U21.2, Part51.HV, Part53.VDD, Q3.source
  N47: Q2.gate, R12.Pin_0
  N48: U21.1, Part51.B1
  N49: Q3.gate, U23.2, R35.Pin_0, R35.Pin_1
  N50: U23.1, R34.Pin_0, R34.Pin_1

notes:
  Green > TTL Laser Diode control
  Pink > 5v+
  i2c > LiDAR unit
  Fold along this edge
  |
  ADC and breakout layer for dust sensor
  GPIOs are PWM for sensor light source and fan
  Fan is the 5v and GND next to the MOSFET
  MCP23017
  Orange are interrupt pins
  Right Bank A - INTA on top
  Left Bank B - INTB on bottom

custom parts:
  MCP23017 I2C I/O Expander: The MCP23017 uses two i2c pins (these can be shared with other i2c devices), and in exchange gives you 16 general purpose pins. You can set each of 16 pins to be input, output, input with a pullup or open drain. There's even the ability to get an interrupt via an external pin when any of the inputs change so you don't have to keep polling the chip.
  Adafruit TCA9548A: You just found the perfect I2C sensor, and you want to wire up two or three or more of them to your Arduino when you realize "Uh oh, this chip has a fixed I2C address, and from what I know about I2C, you cannot have two devices with the same address on the same SDA/SCL pins!" Are you out of luck? You would be, if you didn't have this ultra-cool TCA9548A 1-to-8 I2C multiplexer! Finally, a way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
  Adafruit TSL2591: When the future is dazzlingly-bright, this ultra-high-range luminosity sensor will help you measure it. The TSL2591 luminosity sensor is an advanced digital light sensor, ideal for use in a wide range of light situations. Compared to low cost CdS cells, this sensor is more precise, allowing for exact lux calculations and can be configured for different gain/timing ranges to detect light ranges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
  Adafruit VEML6075 UV Sensor Breakout: This little sensor is a great way to add UVA and UVB light sensing to any microcontroller project. The VEML6075 from Vishay has both true UVA and UVB band light sensors and an I2C-controlled ADC that will take readings and integrate them. The sensor also comes with calibration registers so you can easily convert the UVA/UVB readings into the UV Index. Compared to our other UV sensors, this one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
  Adafruit TCS34725 RGB Color Sensor: Your electronics can now see in dazzling color with this lovely color light sensor. We found the best color sensor on the market, the TCS34725, which has RGB and Clear light sensing elements. An IR blocking filter, integrated on-chip and localized to the color sensing photodiodes, minimizes the IR spectral component of the incoming light and allows color measurements to be made accurately. The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
  Adafruit VL6180X Time of Flight Distance Sensor: The VL6180X is a Time of Flight distance sensor like no other you've used! The sensor contains a very tiny invisible laser source, and a matching sensor. The VL6180X can detect the "time of flight", or how long the light has taken to bounce back to the sensor. Since it uses a very narrow light source, it is good for determining distance of only the surface directly in front of it. Unlike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
  Adafruit SHT31-D Sensirion Temperature/Humidity Sensor: Sensirion Temperature/Humidity sensors are some of the finest & highest-accuracy devices you can get. And, finally we have some that have a true I2C interface for easy reading. The SHT31-D sensor has an excellent ±2% relative humidity and ±0.3°C accuracy for most uses. Unlike earlier SHT sensors, this sensor has a true I2C interface, and (bonus!) even with two address options. It also is 3V or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
  9-DOF Absolute Orientation IMU Fusion Breakout - BNO055: A MEMS accelerometer, magnetometer and gyroscope on a single die with a high speed ARM Cortex-M0 based processor to digest all the sensor data, abstract the sensor fusion and real time requirements away, and spit out data you can use in quaternions, Euler angles or vectors.
  TXB0104 4-channel Bi-Directional Level Shifter: Because the Arduino (and Basic Stamp) are 5V devices, and most modern sensors, displays, flash cards and modes are 3.3V-only, many makers find that they need to perform level shifting/conversion to protect the 3.3V device from 5V. Although one can use resistors to make a divider, for high speed transfers, the resistors can add a lot of slew and cause havoc that is tough to debug. For that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
  Adafruit ADS1115 16Bit I2C ADC: For microcontrollers without an analog-to-digital converter or when you want a higher-precision ADC, the ADS1115 provides 16-bit precision at 860 samples/second over I2C. The chip can be configured as 4 single-ended input channels, or two differential channels. As a nice bonus, it even includes a programmable gain amplifier, up to x16, to help boost up smaller single/differential signals to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
