# Fritzing sketch power-circuit-mini-mint (saved by Fritzing 0.9.3b)
breadboards: 1

parts:
  Part5 = Adafruit PowerBoost 1000C [part_number="Adafruit #2465"]
  MCU2 = Raspberry Pi Zero
  BATT2 = LiPoly Battery (1300mAh)
  Part7 = Adafruit AT42QT1010 Standalone Momentary Capacitive Touch Sensor [part_number="Adafruit #1374"]
  R7 = Resistor [tolerance=±5% resistance=10k package=THT]
  Q8 = NPN-Transistor [package="TO92 [THT]"]
  C3 = Capacitor [package=cap-pth-small2]
  C4 = Capacitor [package=cap-pth-small2]
  Q9 = NPN-Transistor [package="TO92 [THT]"]
  R8 = Resistor [tolerance=±5% resistance=100k package=THT]
  R9 = Resistor [tolerance=±5% resistance=100k package=THT]
  Q10 = NPN-Transistor [package="TO92 [THT]"]
  Q11 = NPN-Transistor [package="TO92 [THT]"]
  R10 = Resistor [tolerance=±5% resistance=100k package=THT]
  Part6 = INA219 High Side DC Current Sensor Breakout [part_number=904]
  S2 = Momentary Switch [package=ksa_sealed_tac_switch]
  JP1 = USB_MICROB_PLUG [package=micro-b-th]
  U1 = Molex Picoblade Series Header [part_number=0533980571 package=Picoblade-53398-0571]
  U2 = Molex Picoblade Series Header [part_number=0533980571 package=Picoblade-53398-0571]

nets:
  N1: Part5.VLIPO, Part6.VIN-
  N2: Part5.ENABLE, Q11.C
  GND: Part5.GND, BATT2.negative, Part7.GND, C4.1, Q9.E, Q11.E, Part6.GND, JP1.GND
  VCC: Part5.5.0V, Part6.VCC, JP1.VCC
  N3: MCU2.pin_3, U2.1
  N4: MCU2.pin_5, U2.2
  N5: MCU2.pin_10, S2.3, U2.4
  N6: MCU2.pin_14, MCU2.pin_34, MCU2.pin_39, S2.1, U2.5
  N7: MCU2.pin_17, U2.3
  N8: BATT2.positive, Part7.VDD, R9.Pin_0, Part6.VIN+
  N9: Part7.OUT, R7.Pin_0, R8.Pin_0
  N10: R7.Pin_1, Q8.B, C3.2
  N11: Q8.E, C3.1, U1.4
  N12: Q8.C, U1.5
  N13: C4.2, Q9.B, R8.Pin_1
  N14: Q9.C, R9.Pin_1, Q10.C, Q11.B
  N15: Q10.B, R10.Pin_1
  N16: R10.Pin_0, U1.3
  N17: Part6.SCL, U1.2
  N18: Part6.SDA, U1.1

custom parts:
  Adafruit PowerBoost 1000C: PowerBoost 1000C is the perfect power supply for your portable project! With a built-in load-sharing battery charger circuit, you'll be able to keep your power-hungry project running even while recharging the battery! This little DC/DC boost converter module can be powered by any 3.7V LiIon/LiPoly battery, and convert the battery output to 5.2V DC for running your 5V projects.
  LiPoly Battery (1300mAh): Lithium Ion Polymer Battery (1300mAh)
  Adafruit AT42QT1010 Standalone Momentary Capacitive Touch Sensor: This breakout board is the simplest way to create a project with a single "momentary" capacitive touch sensor. No microcontroller is required here - just power with 1.8 to 5.5VDC and touch the pad to activate the sensor. When a capacitive load is detected (e.g. a person touches the sensor-pad area) the red LED lights up and the output pin goes high. You can also solder a wire to the middle pad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
  INA219 High Side DC Current Sensor Breakout: This breakout board will solve all your power-monitoring problems. Instead of struggling with two multimeters, you can just use the handy INA219B chip on this breakout to both measure both the high side voltage and DC current draw over I2C with 1% precision. Most current-measuring devices such as our current panel meter are only good for low side measuring. That means that unless you want to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
