# Fritzing sketch power-circuit-trinketm0 (saved by Fritzing 0.9.3b)
breadboards: 1

parts:
  Part2 = INA219 High Side DC Current Sensor Breakout [part_number=904]
  MCU1 = Raspberry Pi Zero
  BATT1 = LiPoly Battery (1300mAh)
  Part3 = Adafruit AT42QT1010 Standalone Momentary Capacitive Touch Sensor [part_number="Adafruit #1374"]
  Part4 = Adafruit PowerBoost 1000C [part_number="Adafruit #2465"]
  Part7 = Adafruit Trinket M0 [part_number="Adafruit #3500"]
  Q8 = NPN-Transistor [package="TO92 [THT]"]
  C3 = Capacitor [package=cap-pth-small2]
  Q9 = NPN-Transistor [package="TO92 [THT]"]
  C4 = Capacitor [package=cap-pth-small2]
  R9 = Resistor [tolerance=±5% resistance=100k package=THT]
  R10 = Resistor [tolerance=±5% resistance=10k package=THT]
  R11 = Resistor [tolerance=±5% resistance=100k package=THT]
  S2 = Momentary Switch [package=ksa_sealed_tac_switch]

nets:
  N1: Part2.VCC, MCU1.pin_4, Part4.5.0V
  GND: Part2.GND, MCU1.pin_6, MCU1.pin_34, MCU1.pin_39, BATT1.negative, Part3.GND, Part4.GND, Q8.E, C3.1
  N2: Part2.VIN-, Part4.VLIPO
  N3: Part2.VIN+, BATT1.positive, Part3.VDD, Part7.VBAT
  N4: MCU1.pin_1, MCU1.pin_17, R11.Pin_1
  N5: MCU1.pin_18, Part7.D1_A0_PA02
  N6: Part3.OUT, R9.Pin_0
  N7: Part4.ENABLE, Part7.D2_A1_PA09_SCL_MISO
  N8: Part7.GND, Q8.C
  N9: Part7.D4_A2_PA06_TXD_MOSI, R10.Pin_1
  N10: Part7.D0_A4_PA08_SDA, R11.Pin_0
  N11: Q8.B, C3.2, R9.Pin_1
  N12: Q9.E, C4.1, S2.1
  N13: Q9.B, C4.2, R10.Pin_0
  N14: Q9.C, S2.3

custom parts:
  INA219 High Side DC Current Sensor Breakout: This breakout board will solve all your power-monitoring problems. Instead of struggling with two multimeters, you can just use the handy INA219B chip on this breakout to both measure both the high side voltage and DC current draw over I2C with 1% precision. Most current-measuring devices such as our current panel meter are only good for low side measuring. That means that unless you want to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
  LiPoly Battery (1300mAh): Lithium Ion Polymer Battery (1300mAh)
  Adafruit AT42QT1010 Standalone Momentary Capacitive Touch Sensor: This breakout board is the simplest way to create a project with a single "momentary" capacitive touch sensor. No microcontroller is required here - just power with 1.8 to 5.5VDC and touch the pad to activate the sensor. When a capacitive load is detected (e.g. a person touches the sensor-pad area) the red LED lights up and the output pin goes high. You can also solder a wire to the middle pad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
  Adafruit PowerBoost 1000C: PowerBoost 1000C is the perfect power supply for your portable project! With a built-in load-sharing battery charger circuit, you'll be able to keep your power-hungry project running even while recharging the battery! This little DC/DC boost converter module can be powered by any 3.7V LiIon/LiPoly battery, and convert the battery output to 5.2V DC for running your 5V projects.
