# Fritzing sketch power-circuit (saved by Fritzing 0.9.3b)
breadboards: 1

parts:
  Part2 = INA219 High Side DC Current Sensor Breakout [part_number=904]
  MCU1 = Raspberry Pi Zero
  BATT1 = LiPoly Battery (1300mAh)
  Part3 = Adafruit AT42QT1010 Standalone Momentary Capacitive Touch Sensor [part_number="Adafruit #1374"]
  Q4 = NPN-Transistor [package="TO92 [THT]"]
  R5 = Resistor [tolerance=±5% resistance=100k package=THT]
  C1 = Capacitor [package=cap-pth-small2]
  Part4 = Adafruit PowerBoost 1000C [part_number="Adafruit #2465"]
  R6 = Resistor [tolerance=±5% resistance=10k package=THT]
  R7 = Resistor [tolerance=±5% resistance=100k package=THT]
  Q5 = NPN-Transistor [package="TO92 [THT]"]
  R8 = Resistor [tolerance=±5% resistance=100k package=THT]
  Q6 = NPN-Transistor [package="TO92 [THT]"]
  Q7 = NPN-Transistor [package="TO92 [THT]"]
  C2 = Capacitor [package=cap-pth-small2]
  S1 = Momentary Switch [package=ksa_sealed_tac_switch]

nets:
  N1: Part2.VCC, MCU1.pin_4, Part4.5.0V
  GND: Part2.GND, MCU1.pin_6, MCU1.pin_34, MCU1.pin_39, BATT1.negative, Part3.GND, Q4.E, C1.1, Part4.GND, Q5.E, Q6.E
  N2: Part2.VIN-, Part4.VLIPO
  N3: Part2.VIN+, BATT1.positive, Part3.VDD, R7.Pin_0
  N4: MCU1.pin_1, MCU1.pin_17, R8.Pin_0
  N5: Part3.OUT, R5.Pin_0, R6.Pin_1
  N6: Q4.B, R5.Pin_1, C1.2
  N7: Q4.C, R7.Pin_1, Q5.C, Q6.B
  N8: Part4.ENABLE, Q6.C
  N9: R6.Pin_0, Q7.B, C2.1
  N10: Q5.B, R8.Pin_1
  N11: Q7.E, C2.2, S1.4
  N12: Q7.C, S1.2

custom parts:
  INA219 High Side DC Current Sensor Breakout: This breakout board will solve all your power-monitoring problems. Instead of struggling with two multimeters, you can just use the handy INA219B chip on this breakout to both measure both the high side voltage and DC current draw over I2C with 1% precision. Most current-measuring devices such as our current panel meter are only good for low side measuring. That means that unless you want to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
  LiPoly Battery (1300mAh): Lithium Ion Polymer Battery (1300mAh)
  Adafruit AT42QT1010 Standalone Momentary Capacitive Touch Sensor: This breakout board is the simplest way to create a project with a single "momentary" capacitive touch sensor. No microcontroller is required here - just power with 1.8 to 5.5VDC and touch the pad to activate the sensor. When a capacitive load is detected (e.g. a person touches the sensor-pad area) the red LED lights up and the output pin goes high. You can also solder a wire to the middle pad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
  Adafruit PowerBoost 1000C: PowerBoost 1000C is the perfect power supply for your portable project! With a built-in load-sharing battery charger circuit, you'll be able to keep your power-hungry project running even while recharging the battery! This little DC/DC boost converter module can be powered by any 3.7V LiIon/LiPoly battery, and convert the battery output to 5.2V DC for running your 5V projects.
